// Digital circuit Lab02.dig as structural Verilog
module Lab02 (
  input  B,
  input  C,
  input  A,
  input  D,
  output Fa,
  output Fb,
  output Fc,
  output Fd,
  output Fe,
  output Fg,
  output Ff
);

  wire A_t, and_1_out, and_2_out, and_3_out, and_4_out, and_5_out, and_6_out, and_7_out, and_8_out,
       and_9_out, and_10_out, and_11_out, and_12_out, B_t, C_t, D_t, Fb_t, Fc_t, Fe_t, Ff_t, Fg_t, not_5_out,
       not_6_out, not_7_out, not_8_out, not_9_out, not_10_out, not_11_out, or_1_out, or_2_out, or_3_out,
       or_4_out, or_5_out, or_6_out;

  not not_1 (A_t, A);
  not not_2 (B_t, B);
  not not_3 (C_t, C);
  not not_4 (D_t, D);
  and and_1 (and_1_out, B_t, D_t);
  and and_2 (and_2_out, C, D_t);
  and and_3 (and_3_out, A_t, C);
  and and_4 (and_4_out, A_t, B, D);
  and and_5 (and_5_out, A, B_t, C_t);
  and and_6 (and_6_out, A, B, C);
  and and_7 (and_7_out, B, C);
  and and_8 (and_8_out, A, not_5_out);
  not not_5 (not_5_out, D);
  and and_9 (and_9_out, not_6_out, C);
  not not_6 (not_6_out, A);
  and and_10 (and_10_out, not_7_out, not_8_out);
  not not_7 (not_7_out, B);
  not not_8 (not_8_out, D);
  and and_11 (and_11_out, not_9_out, B, D);
  not not_9 (not_9_out, A);
  and and_12 (and_12_out, A, not_10_out, not_11_out);
  not not_10 (not_10_out, B);
  not not_11 (not_11_out, C);
  or or_1 (or_1_out, and_1_out, and_2_out);
  or or_2 (or_2_out, and_3_out, and_4_out);
  or or_3 (or_3_out, and_5_out, and_6_out);
  or or_4 (or_4_out, and_7_out, and_8_out);
  or or_5 (or_5_out, and_9_out, and_10_out);
  or or_6 (or_6_out, and_11_out, and_12_out);
  or or_7 (Fa, or_1_out, or_2_out, or_3_out);
  or or_8 (Fd, or_4_out, or_5_out, or_6_out);
  Seven_Seg seven_seg_1 (.a(Fa), .b(Fb_t), .c(Fc_t), .d(Fd), .e(Fe_t), .f(Ff_t), .g(Fg_t), .dp(1'b0));
endmodule
